# Fritzing sketch Design_P1KH001_v2 (saved by Fritzing 0.9.3b)
circuit board: 8.46667cm x 5.64444cm
breadboards: 1

parts:
  Raspberry_Pi_1 = Raspberry Pi 3 [part_number=RPI-3-V1.2]
  R4 = Resistor [tolerance=±5% resistance=3.3k package=THT]
  R3 = Resistor [tolerance=±5% resistance=8.2k package=THT]
  Status_LED = LED - 5mm [color="Red (633nm)" package="5 mm [THT]"]
  R1 = Resistor [tolerance=±5% resistance=220 package=THT]
  P1KH001 = Header 4 [package=screwterminal-3.5mm-4_lock]
  VCC12V = Battery block 9V
  Status_LED1 = LED - 5mm [color="Green (555nm)" package="5 mm [THT]"]
  R2 = Resistor [tolerance=±5% resistance=220 package=THT]

nets:
  N1: Raspberry_Pi_1.GPIO4, R4.Pin_0, R3.Pin_1
  N2: Raspberry_Pi_1.GPIO17, Status_LED.anode
  N3: Raspberry_Pi_1.GPIO27, Status_LED1.anode
  N4: Raspberry_Pi_1.GND, R4.Pin_1, R1.Pin_0, P1KH001.4, VCC12V.-, R2.Pin_0
  N5: R3.Pin_0, P1KH001.2
  N6: Status_LED.cathode, R1.Pin_1
  N7: P1KH001.1, VCC12V.+
  N8: Status_LED1.cathode, R2.Pin_1

notes:
  External Power Supply (12V)
  P1KH001
  A = Schaltausgang Schließer
  Nicht A = Schaltausgang Öffner
  8.2kΩ
  3.3kΩ
  Status
  220Ω
  External Power Supply (10V)
  1=+, 2=A, 3=Â, 4=-
  Belegt
