# Fritzing sketch led-matrix (saved by Fritzing 0.9.3b)
breadboards: 1

parts:
  U1 = NodeMCU V3.0
  8x8_LED_Modul_mit_MAX1 = 8x8 LED Modul mit MAX7219 [package=THT]
  8x8_LED_Modul_mit_MAX2 = 8x8 LED Modul mit MAX7219 [package=THT]
  8x8_LED_Modul_mit_MAX3 = 8x8 LED Modul mit MAX7219 [package=THT]
  8x8_LED_Modul_mit_MAX4 = 8x8 LED Modul mit MAX7219 [package=THT]
  8x8_LED_Modul_mit_MAX5 = 8x8 LED Modul mit MAX7219 [package=THT]
  8x8_LED_Modul_mit_MAX6 = 8x8 LED Modul mit MAX7219 [package=THT]
  8x8_LED_Modul_mit_MAX7 = 8x8 LED Modul mit MAX7219 [package=THT]
  8x8_LED_Modul_mit_MAX8 = 8x8 LED Modul mit MAX7219 [package=THT]
  8x8_LED_Modul_mit_MAX9 = 8x8 LED Modul mit MAX7219 [package=THT]
  8x8_LED_Modul_mit_MAX10 = 8x8 LED Modul mit MAX7219 [package=THT]
  8x8_LED_Modul_mit_MAX11 = 8x8 LED Modul mit MAX7219 [package=THT]
  8x8_LED_Modul_mit_MAX12 = 8x8 LED Modul mit MAX7219 [package=THT]

nets:
  N1: U1.GND#6, U1.GND#13, U1.GND#16, U1.GND#33
  N2: U1.D5, 8x8_LED_Modul_mit_MAX1.CLK_Eingang
  N3: U1.D7, 8x8_LED_Modul_mit_MAX1.DIN_Eingang
  N4: U1.D8, 8x8_LED_Modul_mit_MAX1.CS_Eingang
  N5: U1.VU, 8x8_LED_Modul_mit_MAX1.VCC_Eingang
  N6: U1.GND#41, 8x8_LED_Modul_mit_MAX1.GND_Eingang
  N7: 8x8_LED_Modul_mit_MAX1.VCC_Ausgang, 8x8_LED_Modul_mit_MAX2.VCC_Eingang
  N8: 8x8_LED_Modul_mit_MAX1.GND_Ausgang, 8x8_LED_Modul_mit_MAX2.GND_Eingang
  N9: 8x8_LED_Modul_mit_MAX1.DOUT_Ausgang, 8x8_LED_Modul_mit_MAX2.DIN_Eingang
  N10: 8x8_LED_Modul_mit_MAX1.CS_Ausgang, 8x8_LED_Modul_mit_MAX2.CS_Eingang
  N11: 8x8_LED_Modul_mit_MAX1.CLK_Ausgang, 8x8_LED_Modul_mit_MAX2.CLK_Eingang
  N12: 8x8_LED_Modul_mit_MAX2.VCC_Ausgang, 8x8_LED_Modul_mit_MAX3.VCC_Eingang
  N13: 8x8_LED_Modul_mit_MAX2.GND_Ausgang, 8x8_LED_Modul_mit_MAX3.GND_Eingang
  N14: 8x8_LED_Modul_mit_MAX2.DOUT_Ausgang, 8x8_LED_Modul_mit_MAX3.DIN_Eingang
  N15: 8x8_LED_Modul_mit_MAX2.CS_Ausgang, 8x8_LED_Modul_mit_MAX3.CS_Eingang
  N16: 8x8_LED_Modul_mit_MAX2.CLK_Ausgang, 8x8_LED_Modul_mit_MAX3.CLK_Eingang
  N17: 8x8_LED_Modul_mit_MAX3.VCC_Ausgang, 8x8_LED_Modul_mit_MAX4.VCC_Eingang
  N18: 8x8_LED_Modul_mit_MAX3.GND_Ausgang, 8x8_LED_Modul_mit_MAX4.GND_Eingang
  N19: 8x8_LED_Modul_mit_MAX3.DOUT_Ausgang, 8x8_LED_Modul_mit_MAX4.DIN_Eingang
  N20: 8x8_LED_Modul_mit_MAX3.CS_Ausgang, 8x8_LED_Modul_mit_MAX4.CS_Eingang
  N21: 8x8_LED_Modul_mit_MAX3.CLK_Ausgang, 8x8_LED_Modul_mit_MAX4.CLK_Eingang
  N22: 8x8_LED_Modul_mit_MAX4.VCC_Ausgang, 8x8_LED_Modul_mit_MAX5.VCC_Eingang
  N23: 8x8_LED_Modul_mit_MAX4.GND_Ausgang, 8x8_LED_Modul_mit_MAX5.GND_Eingang
  N24: 8x8_LED_Modul_mit_MAX4.DOUT_Ausgang, 8x8_LED_Modul_mit_MAX5.DIN_Eingang
  N25: 8x8_LED_Modul_mit_MAX4.CS_Ausgang, 8x8_LED_Modul_mit_MAX5.CS_Eingang
  N26: 8x8_LED_Modul_mit_MAX4.CLK_Ausgang, 8x8_LED_Modul_mit_MAX5.CLK_Eingang
  N27: 8x8_LED_Modul_mit_MAX5.VCC_Ausgang, 8x8_LED_Modul_mit_MAX6.VCC_Eingang
  N28: 8x8_LED_Modul_mit_MAX5.GND_Ausgang, 8x8_LED_Modul_mit_MAX6.GND_Eingang
  N29: 8x8_LED_Modul_mit_MAX5.DOUT_Ausgang, 8x8_LED_Modul_mit_MAX6.DIN_Eingang
  N30: 8x8_LED_Modul_mit_MAX5.CS_Ausgang, 8x8_LED_Modul_mit_MAX6.CS_Eingang
  N31: 8x8_LED_Modul_mit_MAX5.CLK_Ausgang, 8x8_LED_Modul_mit_MAX6.CLK_Eingang
  N32: 8x8_LED_Modul_mit_MAX6.VCC_Ausgang, 8x8_LED_Modul_mit_MAX7.VCC_Eingang
  N33: 8x8_LED_Modul_mit_MAX6.GND_Ausgang, 8x8_LED_Modul_mit_MAX7.GND_Eingang
  N34: 8x8_LED_Modul_mit_MAX6.DOUT_Ausgang, 8x8_LED_Modul_mit_MAX7.DIN_Eingang
  N35: 8x8_LED_Modul_mit_MAX6.CS_Ausgang, 8x8_LED_Modul_mit_MAX7.CS_Eingang
  N36: 8x8_LED_Modul_mit_MAX6.CLK_Ausgang, 8x8_LED_Modul_mit_MAX7.CLK_Eingang
  N37: 8x8_LED_Modul_mit_MAX7.VCC_Ausgang, 8x8_LED_Modul_mit_MAX8.VCC_Eingang
  N38: 8x8_LED_Modul_mit_MAX7.GND_Ausgang, 8x8_LED_Modul_mit_MAX8.GND_Eingang
  N39: 8x8_LED_Modul_mit_MAX7.DOUT_Ausgang, 8x8_LED_Modul_mit_MAX8.DIN_Eingang
  N40: 8x8_LED_Modul_mit_MAX7.CS_Ausgang, 8x8_LED_Modul_mit_MAX8.CS_Eingang
  N41: 8x8_LED_Modul_mit_MAX7.CLK_Ausgang, 8x8_LED_Modul_mit_MAX8.CLK_Eingang
  N42: 8x8_LED_Modul_mit_MAX8.VCC_Ausgang, 8x8_LED_Modul_mit_MAX9.VCC_Eingang
  N43: 8x8_LED_Modul_mit_MAX8.GND_Ausgang, 8x8_LED_Modul_mit_MAX9.GND_Eingang
  N44: 8x8_LED_Modul_mit_MAX8.DOUT_Ausgang, 8x8_LED_Modul_mit_MAX9.DIN_Eingang
  N45: 8x8_LED_Modul_mit_MAX8.CS_Ausgang, 8x8_LED_Modul_mit_MAX9.CS_Eingang
  N46: 8x8_LED_Modul_mit_MAX8.CLK_Ausgang, 8x8_LED_Modul_mit_MAX9.CLK_Eingang
  N47: 8x8_LED_Modul_mit_MAX9.VCC_Ausgang, 8x8_LED_Modul_mit_MAX10.VCC_Eingang
  N48: 8x8_LED_Modul_mit_MAX9.GND_Ausgang, 8x8_LED_Modul_mit_MAX10.GND_Eingang
  N49: 8x8_LED_Modul_mit_MAX9.DOUT_Ausgang, 8x8_LED_Modul_mit_MAX10.DIN_Eingang
  N50: 8x8_LED_Modul_mit_MAX9.CS_Ausgang, 8x8_LED_Modul_mit_MAX10.CS_Eingang
  N51: 8x8_LED_Modul_mit_MAX9.CLK_Ausgang, 8x8_LED_Modul_mit_MAX10.CLK_Eingang
  N52: 8x8_LED_Modul_mit_MAX10.VCC_Ausgang, 8x8_LED_Modul_mit_MAX11.VCC_Eingang
  N53: 8x8_LED_Modul_mit_MAX10.GND_Ausgang, 8x8_LED_Modul_mit_MAX11.GND_Eingang
  N54: 8x8_LED_Modul_mit_MAX10.DOUT_Ausgang, 8x8_LED_Modul_mit_MAX11.DIN_Eingang
  N55: 8x8_LED_Modul_mit_MAX10.CS_Ausgang, 8x8_LED_Modul_mit_MAX11.CS_Eingang
  N56: 8x8_LED_Modul_mit_MAX10.CLK_Ausgang, 8x8_LED_Modul_mit_MAX11.CLK_Eingang
  N57: 8x8_LED_Modul_mit_MAX11.VCC_Ausgang, 8x8_LED_Modul_mit_MAX12.VCC_Eingang
  N58: 8x8_LED_Modul_mit_MAX11.GND_Ausgang, 8x8_LED_Modul_mit_MAX12.GND_Eingang
  N59: 8x8_LED_Modul_mit_MAX11.DOUT_Ausgang, 8x8_LED_Modul_mit_MAX12.DIN_Eingang
  N60: 8x8_LED_Modul_mit_MAX11.CS_Ausgang, 8x8_LED_Modul_mit_MAX12.CS_Eingang
  N61: 8x8_LED_Modul_mit_MAX11.CLK_Ausgang, 8x8_LED_Modul_mit_MAX12.CLK_Eingang

notes:
  LED Matrix 24x32 (3x LED Matrix 8x32 Module)

custom parts:
  NodeMCU V3.0: ESP8266 based NodeMCU
