# Fritzing sketch Status-Hat (saved by Fritzing 0.9.3b)
breadboards: 1

parts:
  Raspberry_Pi = Raspberry Pi B+
  LED1 = LED - 5mm [color="Blue (430nm)" package="5 mm [THT]"]
  LED3 = LED - 5mm [color="Yellow (595nm)" package="5 mm [THT]"]
  LED4 = LED - 5mm [color="Green (555nm)" package="5 mm [THT]"]
  LED2 = LED - 5mm [color="Red (633nm)" package="5 mm [THT]"]
  S1 = Pushbutton [package="[THT]"]
  R1 = Resistor [tolerance=±5% resistance=330 package="0805 [SMD]"]
  R3 = Resistor [tolerance=±5% resistance=330 package="0805 [SMD]"]
  R4 = Resistor [tolerance=±5% resistance=330 package="0805 [SMD]"]
  R2 = Resistor [tolerance=±5% resistance=330 package="0805 [SMD]"]
  R5 = Resistor [tolerance=±5% resistance=10k package="0805 [SMD]"]

nets:
  N1: Raspberry_Pi.3v3, S1.Pin_1, S1.Pin_2
  N2: Raspberry_Pi.GPIO6, LED4.anode
  N3: Raspberry_Pi.GPIO19, LED1.anode
  N4: Raspberry_Pi.GPIO26, S1.Pin_3, S1.Pin_4, R5.Pin_0
  N5: Raspberry_Pi.GND, R1.Pin_0, R3.Pin_0, R4.Pin_0, R2.Pin_0, R5.Pin_1
  N6: Raspberry_Pi.GPIO20, LED2.anode
  N7: Raspberry_Pi.GPIO16, LED3.anode
  N8: LED1.cathode, R1.Pin_1
  N9: LED3.cathode, R3.Pin_1
  N10: LED4.cathode, R4.Pin_1
  N11: LED2.cathode, R2.Pin_1
